// Logisim project s-mips.circ as structural Verilog: 6 circuits, main circuit S-MIPS Board
module S_MIPS_Board (
  input  DESHABILITAR_DISPATCHER,
  output halt
);

  wire button_1_out, CLK, CS, d_ff_1_q, LCLR, LoadRAM, LoadRAMOn, LW, R_R_W, R_W, ram_dispatcher_1_finished,
       RCS, Reset_out, RST, TTY_EN;
  wire [2:0] KDB;
  wire [3:0] LMask, Mask, ram_1_read_time, ram_1_write_time, RMask;
  wire [6:0] KDB_DATA, TTY_DATA;
  wire [15:0] Addr, LAddr, RAddr;
  wire [31:0] I0, I1, I2, I3, LData, ram_1_data_out_0, ram_1_data_out_1, ram_1_data_out_2, ram_1_data_out_3,
       RI0, RI1, RI2, RI3;

  TTY #(.rows(25), .cols(80)) tty_1 (.data(TTY_DATA), .clk(CLK), .we(TTY_EN), .clr(RST));
  not not_1 (LoadRAMOn, ram_dispatcher_1_finished);
  RAM_Dispatcher ram_dispatcher_1 (
    .WriteTime(ram_1_write_time), .Clock(CLK), .Data(LData), .Address(LAddr), .Mask(LMask),
    .Finished(ram_dispatcher_1_finished), .Write(LW), .CLR(LCLR));
  Keyboard #(.buflen(64)) keyboard_1 (.clk(CLK), .re(KDB[0]), .avail(KDB[2]), .data(KDB_DATA));  // open: clr
  RAM ram_1 (
    .Address(RAddr), .Data_Out_0(ram_1_data_out_0), .Data_Out_1(ram_1_data_out_1),
    .Data_Out_2(ram_1_data_out_2), .Data_Out_3(ram_1_data_out_3), .Data_In_0(RI0), .Data_In_1(RI1),
    .Data_In_2(RI2), .Data_In_3(RI3), .Mask(RMask), .nRead_Write(R_R_W), .Chip_Select(RCS),
    .Read_Time(ram_1_read_time), .Reset(button_1_out), .Write_Time(ram_1_write_time));
  Button button_1 (.out(button_1_out));
  D_Flip_Flop d_ff_1 (.clk(CLK), .D(1'b1), .Q(d_ff_1_q), .reset(Reset_out));  // open: Qn, preset, en
  Button Reset (.out(Reset_out));
  S_MIPS s_mips_1 (
    .Kbd_Enable(KDB[0]), .Address(Addr), .Kbd_Clear(KDB[1]), .Kbd_Available(KDB[2]), .RAM_In_0(I0),
    .Kbd_ASCII_Data(KDB_DATA), .RAM_In_1(I1), .TTY_Enable(TTY_EN), .RAM_In_2(I2), .RAM_In_3(I2),
    .TTY_ASCII_Data(TTY_DATA), .Reset(RST), .RAM_Out_0(ram_1_data_out_0), .Clock(CLK),
    .RAM_Out_1(ram_1_data_out_1), .Stop(halt), .RAM_Out_2(ram_1_data_out_2), .RAM_Out_3(ram_1_data_out_3),
    .Mask(Mask), .Read_Time(ram_1_read_time), .Write_Time(ram_1_write_time), .nRead_Write(R_W),
    .Chip_Select(CS));
  D_Flip_Flop d_ff_2 (.clk(CLK), .D(d_ff_1_q), .Qn(LCLR), .reset(Reset_out));  // open: Q, preset, en
  or or_1 (RST, LCLR, LoadRAM);
  Clock clock_1 (.out(CLK));
  Multiplexer #(.width(32), .enable("false")) multiplexer_1 (.in0(I0), .in1(LData), .out(RI0), .sel(LoadRAM));
  Multiplexer #(.width(32), .enable("false")) multiplexer_2 (.in0(I1), .in1(LData), .out(RI1), .sel(LoadRAM));
  Multiplexer #(.width(32), .enable("false")) multiplexer_3 (.in0(I2), .in1(LData), .out(RI2), .sel(LoadRAM));
  Multiplexer #(.width(32), .enable("false")) multiplexer_4 (.in0(I3), .in1(LData), .out(RI3), .sel(LoadRAM));
  and and_1 (LoadRAM, ~DESHABILITAR_DISPATCHER, LoadRAMOn);  // AND_Gate
  Multiplexer #(.width(16), .enable("false")) multiplexer_5 (.in0(Addr), .in1(LAddr), .out(RAddr), .sel(LoadRAM));
  Multiplexer #(.width(4), .enable("false")) multiplexer_6 (.in0(Mask), .in1(LMask), .out(RMask), .sel(LoadRAM));
  Multiplexer #(.enable("false")) multiplexer_7 (.in0(CS), .in1(LW), .out(RCS), .sel(LoadRAM));
  Multiplexer #(.enable("false")) multiplexer_8 (.in0(R_W), .in1(LW), .out(R_R_W), .sel(LoadRAM));

  // Notes on the sheet:
  //   NO MODIFICAR
  //   Keyboard
endmodule

module RAM (
  input  [15:0] Address,
  input  [31:0] Data_In_0,
  input  [31:0] Data_In_1,
  input  [31:0] Data_In_2,
  input  [31:0] Data_In_3,
  input  [3:0] Mask,
  input  nRead_Write,
  input  Chip_Select,
  input  Reset,
  output [31:0] Data_Out_0,
  output [31:0] Data_Out_1,
  output [31:0] Data_Out_2,
  output [31:0] Data_Out_3,
  output [3:0] Read_Time,
  output [3:0] Write_Time
);

  wire and_2_out, and_3_out, and_4_out, and_5_out, and_6_out, and_7_out, and_8_out, and_9_out, Changed, CLK,
       comparator_2_eq, comparator_3_eq, comparator_4_eq, comparator_5_eq, comparator_6_eq, Count,
       demultiplexer_3_out0, Idle, Idle_q, Load, Load0, Load1, nand_1_out, or_1_out, or_2_out, or_3_out,
       or_4_out, or_5_out, or_6_out, or_7_out, or_8_out, or_9_out, or_10_out, Proc_q, Update_Mem, Zero_Time;
  wire [3:0] counter_1_q, multiplexer_1_out, subtractor_1_out;
  wire [31:0] register_1_q, register_2_q, register_3_q, register_4_q, register_5_q;

  // Probe on 4'b0011
  // Probe on 4'b0010
  Multiplexer #(.width(4), .enable("false")) multiplexer_1 (
    .in0(4'b0011), .in1(4'b0010), .out(multiplexer_1_out), .sel(nRead_Write));
  or or_1 (or_1_out, Idle, Update_Mem);
  or or_2 (or_2_out, ~Chip_Select, Reset);  // OR_Gate
  Subtractor #(.width(4)) subtractor_1 (.a(multiplexer_1_out), .b(4'b0010), .out(subtractor_1_out));  // open: bin, bout
  D_Flip_Flop u_Idle (.clk(CLK), .D(or_1_out), .Q(Idle_q), .preset(or_2_out));  // open: Qn, en, reset
  Demultiplexer #(.enable("false")) demultiplexer_1 (.out0(Idle), .out1(Load0), .in(Idle_q), .sel(Changed));
  // Probe on counter_1_q
  Counter #(.width(4), .max('hf)) counter_1 (
    .load(Load), .D(subtractor_1_out), .count(Count), .Q(counter_1_q), .clk(CLK), .clr(or_3_out));  // open: carry
  or or_3 (or_3_out, ~Chip_Select, Reset);  // OR_Gate
  Comparator #(.width(4), .mode("unsigned")) comparator_1 (
    .a(4'b0000), .b(counter_1_q), .eq(Zero_Time));  // open: gt, lt
  or or_4 (or_4_out, Count, Load0, Load1);
  Register #(.width(32)) register_1 (.D(Data_In_0), .en(Chip_Select), .Q(register_1_q), .clk(CLK), .clr(or_5_out));
  or or_5 (or_5_out, ~Chip_Select, Reset);  // OR_Gate
  Register #(.width(32)) register_2 (.D(Data_In_1), .en(Chip_Select), .Q(register_2_q), .clk(CLK), .clr(or_6_out));
  or or_6 (or_6_out, ~Chip_Select, Reset);  // OR_Gate
  Register #(.width(32)) register_3 (.D(Data_In_2), .en(Chip_Select), .Q(register_3_q), .clk(CLK), .clr(or_7_out));
  or or_7 (or_7_out, ~Chip_Select, Reset);  // OR_Gate
  Register #(.width(32)) register_4 (.D(Data_In_3), .en(Chip_Select), .Q(register_4_q), .clk(CLK), .clr(or_8_out));
  or or_8 (or_8_out, ~Chip_Select, Reset);  // OR_Gate
  Register #(.width(32)) register_5 (
    .D({{11{1'b1}}, nRead_Write, Mask, Address}), .en(Chip_Select), .Q(register_5_q), .clk(CLK),
    .clr(or_9_out));
  or or_9 (or_9_out, ~Chip_Select, Reset);  // OR_Gate
  D_Flip_Flop Proc (.clk(CLK), .D(or_4_out), .Q(Proc_q), .reset(or_10_out));  // open: Qn, preset, en
  or or_10 (or_10_out, ~Chip_Select, Reset);  // OR_Gate
  Demultiplexer #(.enable("false")) demultiplexer_2 (
    .out0(Count), .out1(Update_Mem), .in(demultiplexer_3_out0), .sel(Zero_Time));
  Demultiplexer #(.enable("false")) demultiplexer_3 (
    .out0(demultiplexer_3_out0), .out1(Load1), .in(Proc_q), .sel(Changed));
  Clock clock_1 (.out(CLK));
  Comparator #(.width(32)) comparator_2 (.a(register_1_q), .b(Data_In_0), .eq(comparator_2_eq));  // open: gt, lt
  Comparator #(.width(32)) comparator_3 (.a(register_2_q), .b(Data_In_1), .eq(comparator_3_eq));  // open: gt, lt
  Comparator #(.width(32)) comparator_4 (.a(register_3_q), .b(Data_In_2), .eq(comparator_4_eq));  // open: gt, lt
  Comparator #(.width(32)) comparator_5 (.a(register_4_q), .b(Data_In_3), .eq(comparator_5_eq));  // open: gt, lt
  Comparator #(.width(32)) comparator_6 (
    .a(register_5_q), .b({{11{1'b1}}, nRead_Write, Mask, Address}), .eq(comparator_6_eq));  // open: gt, lt
  nand nand_1 (nand_1_out, comparator_6_eq, comparator_2_eq, comparator_3_eq, comparator_4_eq, comparator_5_eq);
  and and_1 (Changed, nand_1_out, Chip_Select);
  or or_11 (Load, Count, Load1, Load0);
  and and_2 (and_2_out, Mask[0], Update_Mem, nRead_Write);
  and and_3 (and_3_out, Mask[1], Update_Mem, nRead_Write);
  and and_4 (and_4_out, Mask[2], Update_Mem, nRead_Write);
  and and_5 (and_5_out, Mask[3], Update_Mem, nRead_Write);
  RAM_part #(.addrWidth(16), .dataWidth(32), .bus("separate")) ram_1 (
    .addr(Address), .din(Data_In_0), .data(Data_Out_0), .str(and_2_out), .sel(Chip_Select), .clk(CLK),
    .ld(and_6_out), .clr(Reset));
  and and_6 (and_6_out, ~nRead_Write, Idle);  // AND_Gate
  RAM_part #(.addrWidth(16), .dataWidth(32), .bus("separate")) ram_2 (
    .addr(Address), .din(Data_In_1), .data(Data_Out_1), .str(and_3_out), .sel(Chip_Select), .clk(CLK),
    .ld(and_7_out), .clr(Reset));
  and and_7 (and_7_out, ~nRead_Write, Idle);  // AND_Gate
  RAM_part #(.addrWidth(16), .dataWidth(32), .bus("separate")) ram_3 (
    .addr(Address), .din(Data_In_2), .data(Data_Out_2), .str(and_4_out), .sel(Chip_Select), .clk(CLK),
    .ld(and_8_out), .clr(Reset));
  and and_8 (and_8_out, ~nRead_Write, Idle);  // AND_Gate
  RAM_part #(.addrWidth(16), .dataWidth(32), .bus("separate")) ram_4 (
    .addr(Address), .din(Data_In_3), .data(Data_Out_3), .str(and_5_out), .sel(Chip_Select), .clk(CLK),
    .ld(and_9_out), .clr(Reset));
  and and_9 (and_9_out, ~nRead_Write, Idle);  // AND_Gate

  assign Read_Time = 4'b0011;
  assign Write_Time = 4'b0010;

  // Other names for the same wires on the sheet: M0 = Mask[0]; M1 = Mask[1]; M2 = Mask[2]; M3 = Mask[3];
  //   RW = nRead_Write; CLR = Reset; CS = Chip_Select; Load2 = Count

  // Notes on the sheet:
  //   NO MODIFICAR
  //   excepto quizás los valores RT y WT
  //   BANK0
  //   BANK1
  //   BANK2
  //   BANK3
endmodule

module S_MIPS (
  input  Kbd_Available,
  input  [6:0] Kbd_ASCII_Data,
  input  [31:0] RAM_Out_0,
  input  [31:0] RAM_Out_1,
  input  Reset,
  input  [31:0] RAM_Out_2,
  input  Clock,
  input  [31:0] RAM_Out_3,
  input  [3:0] Read_Time,
  input  [3:0] Write_Time,
  output Kbd_Enable,
  output [15:0] Address,
  output Kbd_Clear,
  output TTY_Enable,
  output [6:0] TTY_ASCII_Data,
  output Stop,
  output [31:0] RAM_In_0,
  output [31:0] RAM_In_1,
  output [31:0] RAM_In_2,
  output [31:0] RAM_In_3,
  output [3:0] Mask,
  output nRead_Write,
  output Chip_Select
);

  wire not_1_out, not_2_out, REG_W;
  wire [4:0] REG_SEL;
  wire [31:0] CP, CP_IN, REG_IN, REG_OUT;

  not not_1 (not_1_out, Reset);
  RF rf_1 (.WRITE(REG_W), .IN(REG_IN), .SEL(REG_SEL), .OUT(REG_OUT), .CLK(Clock), .EN(not_1_out), .RST(Reset));
  not not_2 (not_2_out, Reset);
  Register #(.width(32)) u_CP (.D(CP_IN), .en(not_2_out), .Q(CP), .clk(Clock), .clr(Reset));

  // Other names for the same wires on the sheet: CLK = Clock; CLR = Reset; CS = Chip_Select;
  //   KBD_AVAIL = Kbd_Available; KBD_CLR = Kbd_Clear; KBD_DATA[6:0] = Kbd_ASCII_Data; RAM_A[15:0] = Address;
  //   RAM_INPUT_0[31:0] = RAM_In_0; RAM_INPUT_1[31:0] = RAM_In_1; RAM_INPUT_2[31:0] = RAM_In_2;
  //   RAM_INPUT_3[31:0] = RAM_In_3; RAM_MASK[3:0] = Mask; RAM_OUTPUT_0[31:0] = RAM_Out_0;
  //   RAM_OUTPUT_1[31:0] = RAM_Out_1; RAM_OUTPUT_2[31:0] = RAM_Out_2; RAM_OUTPUT_3[31:0] = RAM_Out_3;
  //   RW = nRead_Write; TTY_DATA[6:0] = TTY_ASCII_Data

  // Notes on the sheet:
  //   RAM ADDRESS
  //   DATA FROM RAM
  //   DATA TO RAM
  //   DATA WRITE MASK
  //   RAM TIMING
  //   RAM CONTROL
  //   KEYBOARD
  //   TTY
  //   SEQUENCING
  //   REGISTRY FETCH
endmodule

module RAM_Dispatcher (
  input  [3:0] WriteTime,
  input  Clock,
  input  CLR,
  output [31:0] Data,
  output [15:0] Address,
  output [3:0] Mask,
  output Finished,
  output Write
);

  wire demultiplexer_2_out1, demultiplexer_3_out1, End, IDLE_q, IncAddr, Load, or_1_out, or_2_out, While_q,
       WriteEnd;
  wire [3:0] counter_1_q;
  wire [31:0] CurrentAddress_q;

  Counter #(.width(32), .max('hffffffff)) CurrentAddress (
    .count(IncAddr), .Q({CurrentAddress_q[31:18], Address, CurrentAddress_q[1:0]}), .clk(Clock), .clr(CLR));  // open: load, D, carry
  or or_1 (or_1_out, IncAddr, demultiplexer_3_out1, Finished);
  D_Flip_Flop IDLE (.clk(Clock), .D(or_1_out), .Q(IDLE_q), .preset(CLR));  // open: Qn, en, reset
  Demultiplexer #(.enable("false")) demultiplexer_1 (.out0(Load), .out1(Finished), .in(IDLE_q), .sel(End));
  D_Flip_Flop While (.clk(Clock), .D(or_2_out), .Q(While_q), .reset(CLR));  // open: Qn, preset, en
  or or_2 (or_2_out, Write, Load);
  RAM_part #(.addrWidth(18), .dataWidth(32)) ram_1 (
    .addr({Address, CurrentAddress_q[1:0]}), .data(Data), .clk(Clock));  // open: sel, ld, clr
  Demultiplexer #(.enable("false")) demultiplexer_2 (
    .out0(Write), .out1(demultiplexer_2_out1), .in(While_q), .sel(WriteEnd));
  Decoder #(.select(2)) decoder_1 (
    .out0(Mask[0]), .out1(Mask[1]), .out2(Mask[2]), .out3(Mask[3]), .sel(CurrentAddress_q[1:0]));  // open: en
  Demultiplexer #(.enable("false")) demultiplexer_3 (
    .out0(IncAddr), .out1(demultiplexer_3_out1), .in(demultiplexer_2_out1), .sel(End));
  Counter #(.width(4), .max('hf)) counter_1 (
    .load(Load), .D(WriteTime), .count(Write), .Q(counter_1_q), .clk(Clock));  // open: carry, clr
  Comparator #(.width(32)) comparator_1 (.a(Data), .b({32{1'b1}}), .eq(End));  // open: gt, lt
  Comparator #(.width(4)) comparator_2 (.a(4'b0000), .b(counter_1_q), .eq(WriteEnd));  // open: gt, lt

  // Other names for the same wires on the sheet: CLK = Clock; Count = Write; WT[3:0] = WriteTime
endmodule

module RF (
  input  WRITE,
  input  [31:0] OUT,
  input  [31:0] IN,
  input  [4:0] SEL,
  input  CLK,
  input  EN,
  input  RST
);

  wire W;
  wire [31:0] R1I, R1O, R2I, R2O, R3I, R3O, R4I, R4O, R5I, R5O, R6I, R6O, R7I, R7O, R8I, R8O, R9I, R9O, R10I,
       R10O, R11I, R11O, R12I, R12O, R13I, R13O, R14I, R14O, R15I, R15O, R16I, R16O, R17I, R17O, R18I, R18O,
       R19I, R19O, R20I, R20O, R21I, R21O, R22I, R22O, R23I, R23O, R24I, R24O, R25I, R25O, R26I, R26O, R27I,
       R27O, R28I, R28O, R29I, R29O, R30I, R30O, R31I, R31O;

  and and_1 (W, WRITE, EN);
  Register #(.width(32)) R4 (.D(R4I), .en(EN), .Q(R4O), .clk(CLK), .clr(RST));
  Register #(.width(32)) R1 (.D(R1I), .en(EN), .Q(R1O), .clk(CLK), .clr(RST));
  Register #(.width(32)) R5 (.D(R5I), .en(EN), .Q(R5O), .clk(CLK), .clr(RST));
  Demultiplexer #(.select(5), .width(32)) demultiplexer_1 (
    .out1(R1I), .out2(R2I), .out3(R3I), .out4(R4I), .out5(R5I), .out6(R6I), .out7(R7I), .out8(R8I),
    .out9(R9I), .out10(R10I), .out11(R11I), .out12(R12I), .out13(R13I), .out14(R14I), .out15(R15I),
    .out16(R16I), .out17(R17I), .out18(R18I), .out19(R19I), .out20(R20I), .out21(R21I), .out22(R22I),
    .out23(R23I), .out24(R24I), .out25(R25I), .out26(R26I), .out27(R27I), .out28(R28I), .out29(R29I),
    .out30(R30I), .out31(R31I), .in(IN), .sel(SEL), .en(W));  // open: out0
  Register #(.width(32)) R3 (.D(R3I), .en(EN), .Q(R3O), .clk(CLK), .clr(RST));
  Register #(.width(32)) R2 (.D(R2I), .en(EN), .Q(R2O), .clk(CLK), .clr(RST));
  Register #(.width(32)) R6 (.D(R6I), .en(EN), .Q(R6O), .clk(CLK), .clr(RST));
  Register #(.width(32)) R7 (.D(R7I), .en(EN), .Q(R7O), .clk(CLK), .clr(RST));
  Register #(.width(32)) R8 (.D(R8I), .en(EN), .Q(R8O), .clk(CLK), .clr(RST));
  Register #(.width(32)) R12 (.D(R12I), .en(EN), .Q(R12O), .clk(CLK), .clr(RST));
  Register #(.width(32)) R9 (.D(R9I), .en(EN), .Q(R9O), .clk(CLK), .clr(RST));
  Register #(.width(32)) R13 (.D(R13I), .en(EN), .Q(R13O), .clk(CLK), .clr(RST));
  Register #(.width(32)) R10 (.D(R10I), .en(EN), .Q(R10O), .clk(CLK), .clr(RST));
  Register #(.width(32)) R14 (.D(R14I), .en(EN), .Q(R14O), .clk(CLK), .clr(RST));
  Register #(.width(32)) R11 (.D(R11I), .en(EN), .Q(R11O), .clk(CLK), .clr(RST));
  Register #(.width(32)) R15 (.D(R15I), .en(EN), .Q(R15O), .clk(CLK), .clr(RST));
  Register #(.width(32)) R16 (.D(R16I), .en(EN), .Q(R16O), .clk(CLK), .clr(RST));
  Register #(.width(32)) _20R (.D(R20I), .en(EN), .Q(R20O), .clk(CLK), .clr(RST));
  Register #(.width(32)) R17 (.D(R17I), .en(EN), .Q(R17O), .clk(CLK), .clr(RST));
  Register #(.width(32)) R21 (.D(R21I), .en(EN), .Q(R21O), .clk(CLK), .clr(RST));
  Register #(.width(32)) R18 (.D(R18I), .en(EN), .Q(R18O), .clk(CLK), .clr(RST));
  Register #(.width(32)) R22 (.D(R22I), .en(EN), .Q(R22O), .clk(CLK), .clr(RST));
  Register #(.width(32)) R19 (.D(R19I), .en(EN), .Q(R19O), .clk(CLK), .clr(RST));
  Register #(.width(32)) R23 (.D(R23I), .en(EN), .Q(R23O), .clk(CLK), .clr(RST));
  Register #(.width(32)) R25 (.D(R25I), .en(EN), .Q(R25O), .clk(CLK));  // open: clr
  Register #(.width(32)) R24 (.D(R24I), .en(EN), .Q(R24O), .clk(CLK));  // open: clr
  Register #(.width(32)) R29 (.D(R29I), .en(EN), .Q(R29O), .clk(CLK));  // open: clr
  Register #(.width(32)) R28 (.D(R28I), .en(EN), .Q(R28O), .clk(CLK));  // open: clr
  Register #(.width(32)) R26 (.D(R26I), .en(EN), .Q(R26O), .clk(CLK));  // open: clr
  Register #(.width(32)) R30 (.D(R30I), .en(EN), .Q(R30O), .clk(CLK));  // open: clr
  Register #(.width(32)) R27 (.D(R27I), .en(EN), .Q(R27O), .clk(CLK));  // open: clr
  Register #(.width(32)) R31 (.D(R31I), .en(EN), .Q(R31O), .clk(CLK));  // open: clr
  Multiplexer #(.select(5), .width(32)) multiplexer_1 (
    .in0({32{1'b0}}), .in1(R1O), .in2(R2O), .in3(R3O), .in4(R4O), .in5(R5O), .in6(R6O), .in7(R7O), .in8(R8O),
    .in9(R9O), .in10(R10O), .in11(R11O), .in12(R12O), .in13(R13O), .in14(R14O), .in15(R15O), .in16(R16O),
    .in17(R17O), .in18(R18O), .in19(R19O), .in20(R20O), .in21(R21O), .in22(R22O), .in23(R23O), .in24(R24O),
    .in25(R25O), .in26(R26O), .in27(R27O), .in28(R28O), .in29(R29O), .in30(R30O), .in31(R31O), .out(OUT),
    .sel(SEL), .en(EN));

  // Other names for the same wires on the sheet: ENABLE = EN; INPUT[31:0] = IN; RESET = RST
endmodule

module ALU (
  input  [31:0] IN_A,
  input  [31:0] IN_B,
  input  U,
  input  [2:0] SEL,
  input  CLK,
  input  EN,
  output [31:0] OUT1,
  output [31:0] OUT2,
  output out_9,
  output out_10
);

  wire ADD_CARRY, comparator_1_eq, comparator_2_eq, decoder_1_out0, decoder_1_out1, not_2_out, SUB_CARRY;
  wire [31:0] ADD_OUT, AND_OUT, DIV_OUT1, DIV_OUT_2, MUL_OUT1, MUL_OUT_2, NOR_OUT, OR_OUT, SUB_OUT, XOR_OUT;

  Adder #(.width(32)) adder_1 (.a(IN_A), .b(IN_B), .out(ADD_OUT), .cout(ADD_CARRY));  // open: cin
  Subtractor #(.width(32)) subtractor_1 (.a(IN_A), .b(IN_B), .out(SUB_OUT), .bout(SUB_CARRY));  // open: bin
  Multiplier #(.width(32)) multiplier_1 (.a(IN_A), .b(IN_B), .out(MUL_OUT1), .cout(MUL_OUT_2));  // open: cin
  Divider #(.width(32)) divider_1 (.a(IN_A), .b(IN_B), .out(DIV_OUT1), .rem(DIV_OUT_2));  // open: upper
  Decoder decoder_1 (.out0(decoder_1_out0), .out1(decoder_1_out1), .sel(SEL[2]), .en(EN));
  Multiplexer #(.select(2), .width(32)) multiplexer_1 (
    .in0(ADD_OUT), .in1(SUB_OUT), .in2(MUL_OUT1), .in3(DIV_OUT1), .out(OUT1), .sel(SEL[1:0]),
    .en(decoder_1_out0));
  Multiplexer #(.width(32)) multiplexer_2 (
    .in0(MUL_OUT_2), .in1(DIV_OUT_2), .out(OUT2), .sel(SEL[0]), .en(decoder_1_out0));
  Multiplexer #(.select(2), .width(32)) multiplexer_3 (
    .in0(AND_OUT), .in1(OR_OUT), .in2(NOR_OUT), .in3(XOR_OUT), .out(OUT1), .sel(SEL[1:0]), .en(decoder_1_out1));
  assign AND_OUT = IN_A & IN_B;  // AND_Gate and_1, 32 bits wide
  assign OR_OUT = IN_A | IN_B;  // OR_Gate or_1, 32 bits wide
  assign XOR_OUT = IN_A ^ IN_B;  // XOR_Gate xor_1, 32 bits wide
  assign NOR_OUT = ~OR_OUT;  // NOT_Gate not_1, 32 bits wide
  Comparator #(.width(32)) comparator_1 (.a(OUT2), .b({32{1'b0}}), .eq(comparator_1_eq));  // open: gt, lt
  not not_2 (not_2_out, comparator_1_eq);
  Comparator #(.width(32)) comparator_2 (.a(OUT1), .b(OUT2), .eq(comparator_2_eq));  // open: gt, lt
  and and_2 (out_10, comparator_2_eq, comparator_1_eq);
  Multiplexer #(.select(2)) multiplexer_4 (
    .in0(ADD_CARRY), .in1(SUB_CARRY), .in2(not_2_out), .in3(not_2_out), .out(out_9), .sel(SEL[1:0]), .en(EN));

  // Other names for the same wires on the sheet: CF = out_9; ENABLED = EN; ZF = out_10
endmodule
